// Logisim project real ai alu.circ as structural Verilog: 15 circuits, main circuit Real Alu 2.0
module Real_Alu_2_0 (
  input  [3:0] Selettore,
  input  [7:0] A,
  input  [7:0] B,
  output [7:0] Y,
  output Z,
  output C,
  output N,
  output V
);

  // Probe on A
  // Probe on B
  Real_alu_1_0 real_alu_1_0_1 (.b(B), .a(A), .z(Z), .out_5(Y), .c(C), .n(N), .v(V), .in_3(Selettore));
  // Probe on Y
endmodule

module main (
  input  [7:0] A,
  input  [7:0] B,
  input  [3:0] S,
  output Z,
  output C,
  output N,
  output V,
  output [7:0] out_8
);

  real_alu real_alu_1 (.b(B), .a(A), .z(Z), .out_5(out_8), .c(C), .n(N), .v(V), .in_3(S));
endmodule

module subbbb (
  input  [7:0] a,
  input  [7:0] b,
  output [7:0] S,
  output n,
  output v,
  output c
);

  wire full_adder_1_c, full_adder_2_c, full_adder_3_c, full_adder_4_c, full_adder_5_c, full_adder_6_c,
       full_adder_7_c, not_1_out, not_2_out, not_3_out, not_4_out, not_5_out, not_6_out, not_7_out, not_8_out;

  not not_1 (not_1_out, b[7]);
  not not_2 (not_2_out, b[2]);
  not not_3 (not_3_out, b[4]);
  not not_4 (not_4_out, b[5]);
  not not_5 (not_5_out, b[3]);
  not not_6 (not_6_out, b[6]);
  not not_7 (not_7_out, b[0]);
  not not_8 (not_8_out, b[1]);
  full_adder full_adder_1 (.c0(1'b1), .A(a[0]), .B(not_7_out), .S(S[0]), .C(full_adder_1_c));
  full_adder full_adder_2 (.c0(full_adder_1_c), .A(a[1]), .B(not_8_out), .S(S[1]), .C(full_adder_2_c));
  full_adder full_adder_3 (.c0(full_adder_2_c), .A(a[2]), .B(not_2_out), .S(S[2]), .C(full_adder_3_c));
  full_adder full_adder_4 (.c0(full_adder_3_c), .A(a[3]), .B(not_5_out), .S(S[3]), .C(full_adder_4_c));
  full_adder full_adder_5 (.c0(full_adder_4_c), .A(a[4]), .B(not_3_out), .S(S[4]), .C(full_adder_5_c));
  full_adder full_adder_6 (.c0(full_adder_5_c), .A(a[5]), .B(not_4_out), .S(S[5]), .C(full_adder_6_c));
  full_adder full_adder_7 (.c0(full_adder_6_c), .A(a[6]), .B(not_6_out), .S(S[6]), .C(full_adder_7_c));
  full_adder full_adder_8 (.c0(full_adder_7_c), .A(a[7]), .B(not_1_out), .S(n), .C(c));
  xor xor_1 (v, n, c);

  assign S[7] = n;
endmodule

module in_a_and_in_b (
  input  [7:0] in_1,
  input  [7:0] in_2,
  output [7:0] out_3
);

  assign out_3 = in_1 & in_2;  // AND_Gate and_1, 8 bits wide
endmodule

module in_a_or_in_b (
  input  [7:0] in_1,
  input  [7:0] in_2,
  output [7:0] out_3
);

  assign out_3 = in_1 | in_2;  // OR_Gate or_1, 8 bits wide
endmodule

module not_in_b (
  input  [7:0] in_1,
  output [7:0] out_2
);

  assign out_2 = ~in_1;  // NOT_Gate not_1, 8 bits wide
endmodule

module LSL_in_b (
  input  [7:0] in_1,
  output n,
  output c,
  output [7:0] out_4
);


  assign c = in_1[7];
  assign n = in_1[6];
  assign out_4 = {in_1[6:0], 1'b0};
endmodule

module LSR_IN_B (
  input  [7:0] in_1,
  output c,
  output n,
  output [7:0] out_4
);


  assign c = in_1[0];
  assign n = 1'b0;
  assign out_4 = {1'b0, in_1[7:1]};
endmodule

module sommmm (
  input  [7:0] a,
  input  [7:0] b,
  output [7:0] S,
  output n,
  output v,
  output c
);

  wire full_adder_1_c, full_adder_2_c, full_adder_3_c, full_adder_4_c, full_adder_5_c, full_adder_6_c,
       half_adder_1_c;

  half_adder half_adder_1 (.S(S[0]), .C(half_adder_1_c), .A(a[0]), .B(b[0]));
  full_adder full_adder_1 (.c0(half_adder_1_c), .A(a[1]), .B(b[1]), .S(S[1]), .C(full_adder_1_c));
  full_adder full_adder_2 (.c0(full_adder_1_c), .A(a[2]), .B(b[2]), .S(S[2]), .C(full_adder_2_c));
  full_adder full_adder_3 (.c0(full_adder_2_c), .A(a[3]), .B(b[3]), .S(S[3]), .C(full_adder_3_c));
  full_adder full_adder_4 (.c0(full_adder_3_c), .A(a[4]), .B(b[4]), .S(S[4]), .C(full_adder_4_c));
  full_adder full_adder_5 (.c0(full_adder_4_c), .A(a[5]), .B(b[5]), .S(S[5]), .C(full_adder_5_c));
  full_adder full_adder_6 (.c0(full_adder_5_c), .A(a[6]), .B(b[6]), .S(S[6]), .C(full_adder_6_c));
  full_adder full_adder_7 (.c0(full_adder_6_c), .A(a[7]), .B(b[7]), .S(n), .C(c));
  xor xor_1 (v, n, c);

  assign S[7] = n;
endmodule

module half_adder (
  input  A,
  input  B,
  output S,
  output C
);

  xor xor_1 (S, A, B);
  and and_1 (C, A, B);
endmodule

module full_adder (
  input  c0,
  input  A,
  input  B,
  output S,
  output C
);

  wire and_1_out, and_2_out, and_3_out, xor_1_out;

  and and_1 (and_1_out, c0, A);
  and and_2 (and_2_out, A, B);
  and and_3 (and_3_out, c0, B);
  xor xor_1 (xor_1_out, A, B);
  or or_1 (C, and_1_out, and_2_out, and_3_out);
  xor xor_2 (S, xor_1_out, c0);
endmodule

module incr (
  input  [7:0] B,
  output [7:0] S,
  output n,
  output v,
  output c
);

  sommmm sommmm_1 (.a(B), .b(8'h1), .S(S), .c(c), .n(n), .v(v));
endmodule

module decr (
  input  [7:0] B,
  output [7:0] s,
  output n,
  output v,
  output c
);

  subbbb subbbb_1 (.a(B), .b(8'h1), .S(s), .c(c), .n(n), .v(v));
endmodule

module real_alu (
  input  [7:0] b,
  input  [7:0] a,
  input  [3:0] in_3,
  output z,
  output [7:0] out_5,
  output c,
  output n,
  output v
);

  wire _1, _2, _3, _4, _5, _6, _8, _9, _10, _11, _12, _13, _16, _17, _18, _19;
  wire [7:0] decr_1_s, in_a_and_in_b_1_out_3, in_a_or_in_b_1_out_3, incr_1_s, lsl_in_b_1_out_4,
       lsr_in_b_1_out_4, not_in_b_1_out_2, sommmm_1_s, subbbb_1_s;

  LSL_in_b lsl_in_b_1 (.in_1(b), .c(_1), .out_4(lsl_in_b_1_out_4), .n(_8));
  in_a_and_in_b in_a_and_in_b_1 (.in_1(b), .in_2(a), .out_3(in_a_and_in_b_1_out_3));
  in_a_or_in_b in_a_or_in_b_1 (.in_1(b), .in_2(a), .out_3(in_a_or_in_b_1_out_3));
  not_in_b not_in_b_1 (.in_1(b), .out_2(not_in_b_1_out_2));
  LSR_IN_B lsr_in_b_1 (.c(_2), .in_1(b), .n(_9), .out_4(lsr_in_b_1_out_4));
  incr incr_1 (.B(b), .S(incr_1_s), .n(_12), .v(_18), .c(_5));
  decr decr_1 (.B(b), .s(decr_1_s), .n(_13), .v(_19), .c(_6));
  sommmm sommmm_1 (.a(b), .b(a), .S(sommmm_1_s), .c(_3), .n(_10), .v(_16));
  subbbb subbbb_1 (.a(b), .b(a), .S(subbbb_1_s), .c(_4), .n(_11), .v(_17));
  Multiplexer #(.select(4), .width(8)) multiplexer_1 (
    .in0(in_a_and_in_b_1_out_3), .in1(in_a_or_in_b_1_out_3), .in2(not_in_b_1_out_2), .in3(lsl_in_b_1_out_4),
    .in4(lsr_in_b_1_out_4), .in5(sommmm_1_s), .in6(subbbb_1_s), .in7(incr_1_s), .in8(decr_1_s), .in9(a),
    .in10(out_5), .in11(out_5), .in12(out_5), .in13(out_5), .in14(out_5), .in15(out_5), .out(out_5),
    .sel(in_3));  // open: en
  nor nor_1 (z, out_5[0], out_5[1], out_5[2], out_5[3], out_5[4], out_5[5], out_5[6], out_5[7]);
  Multiplexer #(.select(4)) multiplexer_2 (
    .in0(1'b0), .in1(1'b0), .in2(1'b0), .in3(_1), .in4(_2), .in5(_3), .in6(_4), .in7(_5), .in8(_6),
    .in9(1'b0), .in10(c), .in11(c), .in12(c), .in13(c), .in14(c), .in15(c), .out(c), .sel(in_3));  // open: en
  Multiplexer #(.select(4)) multiplexer_3 (
    .in0(1'b0), .in1(1'b0), .in2(1'b0), .in3(_8), .in4(_9), .in5(_10), .in6(_11), .in7(_12), .in8(_13),
    .in9(a[7]), .in10(n), .in11(n), .in12(n), .in13(n), .in14(n), .in15(n), .out(n), .sel(in_3));  // open: en
  Multiplexer #(.select(4)) multiplexer_4 (
    .in0(1'b0), .in1(1'b0), .in2(1'b0), .in3(1'b0), .in4(1'b0), .in5(_16), .in6(_17), .in7(_18), .in8(_19),
    .in9(1'b0), .in10(v), .in11(v), .in12(v), .in13(v), .in14(v), .in15(v), .out(v), .sel(in_3));  // open: en

  // Other names for the same wires on the sheet: _7 = c; _15 = n; _20 = v; _14 = a[7]; c_t[7:0] = out_5;
  //   x[3:0] = in_3
endmodule

module Real_alu_1_0 (
  input  [7:0] b,
  input  [7:0] a,
  input  [3:0] in_3,
  output z,
  output [7:0] out_5,
  output c,
  output n,
  output v
);

  wire _1, _2, _3, _4, _5, _6, _8, _9, _10, _11, _12, _13, _16, _17, _18, _19;
  wire [7:0] decr_1_s, in_a_and_in_b_1_out_3, in_a_or_in_b_1_out_3, incr_1_s, lsl_in_b_1_out_4,
       lsr_in_b_1_out_4, not_in_b_1_out_2, sommmm_1_s, subbbb_1_s;

  LSL_in_b lsl_in_b_1 (.in_1(b), .c(_1), .out_4(lsl_in_b_1_out_4), .n(_8));
  in_a_and_in_b in_a_and_in_b_1 (.in_1(b), .in_2(a), .out_3(in_a_and_in_b_1_out_3));
  in_a_or_in_b in_a_or_in_b_1 (.in_1(b), .in_2(a), .out_3(in_a_or_in_b_1_out_3));
  not_in_b not_in_b_1 (.in_1(b), .out_2(not_in_b_1_out_2));
  LSR_IN_B lsr_in_b_1 (.c(_2), .in_1(b), .n(_9), .out_4(lsr_in_b_1_out_4));
  incr incr_1 (.B(b), .S(incr_1_s), .n(_12), .v(_18), .c(_5));
  decr decr_1 (.B(b), .s(decr_1_s), .n(_13), .v(_19), .c(_6));
  sommmm sommmm_1 (.a(b), .b(a), .S(sommmm_1_s), .c(_3), .n(_10), .v(_16));
  subbbb subbbb_1 (.a(b), .b(a), .S(subbbb_1_s), .c(_4), .n(_11), .v(_17));
  Multiplexer #(.select(4), .width(8)) multiplexer_1 (
    .in0(in_a_and_in_b_1_out_3), .in1(in_a_or_in_b_1_out_3), .in2(not_in_b_1_out_2), .in3(lsl_in_b_1_out_4),
    .in4(lsr_in_b_1_out_4), .in5(sommmm_1_s), .in6(subbbb_1_s), .in7(incr_1_s), .in8(decr_1_s), .in9(a),
    .in10(out_5), .in11(out_5), .in12(out_5), .in13(out_5), .in14(out_5), .in15(out_5), .out(out_5),
    .sel(in_3));  // open: en
  nor nor_1 (z, out_5[0], out_5[1], out_5[2], out_5[3], out_5[4], out_5[5], out_5[6], out_5[7]);
  Multiplexer #(.select(4)) multiplexer_2 (
    .in0(1'b0), .in1(1'b0), .in2(1'b0), .in3(_1), .in4(_2), .in5(_3), .in6(_4), .in7(_5), .in8(_6),
    .in9(1'b0), .in10(c), .in11(c), .in12(c), .in13(c), .in14(c), .in15(c), .out(c), .sel(in_3));  // open: en
  Multiplexer #(.select(4)) multiplexer_3 (
    .in0(1'b0), .in1(1'b0), .in2(1'b0), .in3(_8), .in4(_9), .in5(_10), .in6(_11), .in7(_12), .in8(_13),
    .in9(a[7]), .in10(n), .in11(n), .in12(n), .in13(n), .in14(n), .in15(n), .out(n), .sel(in_3));  // open: en
  Multiplexer #(.select(4)) multiplexer_4 (
    .in0(1'b0), .in1(1'b0), .in2(1'b0), .in3(1'b0), .in4(1'b0), .in5(_16), .in6(_17), .in7(_18), .in8(_19),
    .in9(1'b0), .in10(v), .in11(v), .in12(v), .in13(v), .in14(v), .in15(v), .out(v), .sel(in_3));  // open: en

  // Other names for the same wires on the sheet: _7 = c; _15 = n; _20 = v; _14 = a[7]; c_t[7:0] = out_5;
  //   x[3:0] = in_3
endmodule
